# Fritzing sketch Ventilator_Main- Clean PCB (saved by Fritzing 0.8.7b)
circuit board: 11.4759cm x 9.76025cm
circuit board: 7.85cm x 7.81656cm
breadboards: 1

parts:
  Arduino_UNO = Arduino Uno (Rev3)
  LCD2 = LCD screen
  Buzzer1 = Piezo Speaker
  R16 = Resistor [tolerance=±5% resistance=220 package=THT]
  ON/OFF_PUSH = Pushbutton [package="[THT]"]
  R17 = Resistor [tolerance=±5% resistance=220 package=THT]
  POT-LCD = Trimmer Potentiometer [maximum_resistance=10kΩ package=THT]
  POT1 = Rotary Potentiometer (Small) [maximum_resistance=100kΩ package=THT]
  POT2 = Rotary Potentiometer (Small) [maximum_resistance=100kΩ package=THT]
  POT3 = Rotary Potentiometer (Small) [maximum_resistance=100kΩ package=THT]
  R22 = Resistor [tolerance=±5% resistance=220 package=THT]
  Arduino_Micro = Arduino Micro (Rev3)
  Emergency_Sw = Toggle Switch [package=THT]
  R23 = Resistor [tolerance=±5% resistance=220 package=THT]
  R24 = Resistor [tolerance=±5% resistance=220 package=THT]
  Limit_Sw = Toggle Switch [package=THT]
  LED2 = LED - 5mm [color="Red (633nm)" package="5 mm [THT]"]
  R26 = Resistor [tolerance=±5% resistance=220 package=THT]
  24V_Supply = Power plug
  M2 = Stepper Motor - Bipolar  # not connected
  Relay = Relay [part_number=FRS1B-S package=THT]
  R25 = Resistor [tolerance=±5% resistance=220 package=THT]
  LM2596 = RioRand LM2596
  LM2596-2 = RioRand LM2596
  Buzzer2 = Piezo Speaker
  Vin = Header 1 [package=smtso-256-et]

nets:
  N1: Arduino_UNO.A0, POT1.wiper
  N2: Arduino_UNO.A1, POT2.wiper
  N3: Arduino_UNO.A2, POT3.wiper
  N4: Arduino_UNO.A5/SCL, Arduino_Micro.A3, Limit_Sw.COM
  N5: Arduino_UNO.D8, LCD2.DB7
  N6: Arduino_UNO.D9_PWM, LCD2.DB6
  N7: Arduino_UNO.D10_PWM/SS, LCD2.DB5
  N8: Arduino_UNO.D11_PWM/MOSI, LCD2.DB4
  N9: Arduino_UNO.D12/MISO, LCD2.E
  N10: Arduino_UNO.D13/SCK, LCD2.RS
  GND: Arduino_UNO.GND, LCD2.VSS, LCD2.R/W, R16.Pin_0, R17.Pin_0, R25.Pin_1
  N11: Arduino_UNO.D3_PWM, ON/OFF_PUSH.Pin_3, ON/OFF_PUSH.Pin_4, R17.Pin_1
  N12: Arduino_UNO.D7, Buzzer1.pin2
  5V: Arduino_UNO.5V, LCD2.VDD, ON/OFF_PUSH.Pin_1, ON/OFF_PUSH.Pin_2, POT-LCD.leg1, POT1.leg1, POT2.leg1, POT3.leg1, R22.Pin_0
  N13: Arduino_UNO.VIN, LM2596-2.Pin_2, Vin.1
  N14: LCD2.V0, POT-LCD.wiper
  N15: LCD2.LED+, R22.Pin_1
  N16: LCD2.LED-, POT-LCD.leg2, POT1.leg2, POT2.leg2, POT3.leg2
  N17: Buzzer1.pin1, R16.Pin_1
  N18: Arduino_Micro.GND, R23.Pin_1, R24.Pin_1, R26.Pin_1, Relay.COIL2, LM2596.Pin_3, LM2596-2.Pin_3
  N19: Arduino_Micro.D2/SDA, Emergency_Sw.COM
  N20: Arduino_Micro.D8_PWM/A8, LED2.anode
  N21: Arduino_Micro.D9_PWM/A9, Relay.COIL1
  N22: Arduino_Micro.D10_PWM/A10, Buzzer2.pin2
  N23: Arduino_Micro.VIN, LM2596.Pin_2
  N24: Emergency_Sw.L1, R23.Pin_0
  N25: R24.Pin_0, Buzzer2.pin1
  N26: Limit_Sw.L1, R25.Pin_0
  N27: LED2.cathode, R26.Pin_0
  N28: 24V_Supply.VCC, Relay.C1, Relay.C2, LM2596.Pin_0
  N29: 24V_Supply.GND, LM2596.Pin_1, LM2596-2.Pin_1
  N30: Relay.A, LM2596-2.Pin_0

notes:
  B- B+ A- A+ GND VCC
  TB6600
  pul+ pul- dir+ dir- EN
