# Fritzing sketch Ventilator_Main-Schematic (saved by Fritzing 0.8.7b)
breadboards: 1

parts:
  Part4 = Arduino Uno (Rev3)
  LCD2 = LCD screen
  J3 = Piezo Speaker
  R16 = Resistor [tolerance=±5% resistance=220 package=THT]
  S4 = Pushbutton [package="[THT]"]
  R17 = Resistor [tolerance=±5% resistance=220 package=THT]
  R18 = Trimmer Potentiometer [maximum_resistance=10kΩ package=THT]
  R19 = Rotary Potentiometer (Small) [maximum_resistance=100kΩ package=THT]
  R20 = Rotary Potentiometer (Small) [maximum_resistance=100kΩ package=THT]
  R21 = Rotary Potentiometer (Small) [maximum_resistance=100kΩ package=THT]
  R22 = Resistor [tolerance=±5% resistance=220 package=THT]
  Part5 = Arduino Micro (Rev3)
  S5 = Toggle Switch [package=THT]
  R23 = Resistor [tolerance=±5% resistance=220 package=THT]  # not connected
  J4 = Piezo Speaker
  R24 = Resistor [tolerance=±5% resistance=220 package=THT]  # not connected
  S6 = Toggle Switch [package=THT]
  LED2 = LED - 5mm [color="Red (633nm)" package="5 mm [THT]"]
  R26 = Resistor [tolerance=±5% resistance=220 package=THT]  # not connected
  24V_Supply = Power plug
  M2 = Stepper Motor - Bipolar  # not connected
  K2 = Relay [part_number=FRS1B-S package=THT]
  R25 = Resistor [tolerance=±5% resistance=220 package=THT]
  LM2596 = RioRand LM2596
  LM2597 = RioRand LM2596

nets:
  N1: Part4.A0, R19.wiper
  N2: Part4.A1, R20.wiper
  N3: Part4.A2, R21.wiper
  N4: Part4.A5/SCL, Part5.A3, S6.COM
  N5: Part4.D8, LCD2.DB7
  N6: Part4.D9_PWM, LCD2.DB6
  N7: Part4.D10_PWM/SS, LCD2.DB5
  N8: Part4.D11_PWM/MOSI, LCD2.DB4
  N9: Part4.D12/MISO, LCD2.E
  N10: Part4.D13/SCK, LCD2.RS
  GND: Part4.GND, R16.Pin_0, R17.Pin_0, R18.leg1, R19.leg1, R20.leg1, R21.leg1, Part5.GND, K2.COIL2, R25.Pin_1, LM2596.Pin_3, LM2597.Pin_3
  N11: Part4.D3_PWM, S4.Pin_3, S4.Pin_4, R17.Pin_1
  N12: Part4.D7, J3.pin2
  5V: Part4.5V, LCD2.VDD, S4.Pin_1, S4.Pin_2, R18.leg2, R19.leg2, R20.leg2, R21.leg2
  N13: Part4.VIN, LM2597.Pin_2
  N14: LCD2.V0, R18.wiper
  N15: LCD2.LED+, R22.Pin_1
  N16: J3.pin1, R16.Pin_1
  N17: Part5.D2/SDA, S5.COM
  N18: Part5.D8_PWM/A8, LED2.anode
  N19: Part5.D9_PWM/A9, K2.COIL1
  N20: Part5.D10_PWM/A10, J4.pin2
  N21: Part5.VIN, LM2596.Pin_2
  N22: S6.L1, R25.Pin_0
  N23: 24V_Supply.VCC, K2.C2, LM2596.Pin_0
  N24: 24V_Supply.GND, LM2596.Pin_1, LM2597.Pin_1
  N25: K2.A, LM2597.Pin_0

notes:
  B- B+ A- A+ GND VCC
  TB6600 Controller
  pul+ pul- dir+ dir- EN
